# Fritzing sketch ESP8266_Weather_Station (saved by Fritzing 0.9.3b)
breadboards: 1

parts:
  BMP180 = Barometric Pressure Sensor - BMP180 Breakout (GY-68)
  Error_LED = LED - 3mm [color="Red (633nm)" package="3 mm [THT]"]
  R1 = Resistor [tolerance=±5% resistance=220 package="2512 [SMD]"]
  Activity_LED = LED - 3mm [color="Yellow (574nm)" package="3 mm [THT]"]
  Ok_LED = LED - 3mm [color="Red (633nm)" package="3 mm [THT]"]
  R2 = Resistor [tolerance=±5% resistance=220 package="2512 [SMD]"]
  R3 = Resistor [tolerance=±5% resistance=220 package="2512 [SMD]"]
  DHT22 = Humidity and Temperature Sensor RHT03
  ESP8266 = SparkFun ESP8266 Thing

nets:
  VCC: BMP180.VCC, DHT22.Vcc, ESP8266.VCC
  GND: BMP180.GND, R1.Pin_0, R2.Pin_0, R3.Pin_0, DHT22.GND_1, DHT22.GND_2, ESP8266.GND
  N1: BMP180.SCL, ESP8266.GPIO5
  N2: BMP180.SDA, ESP8266.GPIO4
  N3: Error_LED.cathode, R1.Pin_1
  N4: Error_LED.anode, ESP8266.GPIO12
  N5: Activity_LED.cathode, R3.Pin_1
  N6: Activity_LED.anode, ESP8266.GPIO15
  N7: Ok_LED.cathode, R2.Pin_1
  N8: Ok_LED.anode, ESP8266.GPIO14
  N9: DHT22.Data-signal, ESP8266.GPIO13
